// Logisim project 2S Complement.circ as structural Verilog: 2 circuits, main circuit main
module main (
  input  [3:0] in_1,
  output [3:0] out_2
);

  wire half_adder_2_out_4, half_adder_3_out_4, half_adder_4_out_4, not_1_out, not_2_out, not_3_out, not_4_out;

  not not_1 (not_1_out, in_1[3]);
  half_adder half_adder_1 (.in_1(not_1_out), .in_2(half_adder_2_out_4), .out_3(out_2[3]));  // open: out_4
  not not_2 (not_2_out, in_1[2]);
  half_adder half_adder_2 (.in_1(not_2_out), .in_2(half_adder_3_out_4), .out_3(out_2[2]), .out_4(half_adder_2_out_4));
  not not_3 (not_3_out, in_1[1]);
  half_adder half_adder_3 (.in_1(not_3_out), .in_2(half_adder_4_out_4), .out_3(out_2[1]), .out_4(half_adder_3_out_4));
  half_adder half_adder_4 (.in_1(1'b1), .in_2(not_4_out), .out_3(out_2[0]), .out_4(half_adder_4_out_4));
  not not_4 (not_4_out, in_1[0]);
endmodule

module half_adder (
  input  in_1,
  input  in_2,
  output out_3,
  output out_4
);

  xor xor_1 (out_3, in_1, in_2);
  and and_1 (out_4, in_1, in_2);
endmodule
