// Logisim project 4-bit adder and subtractor final.circ as structural Verilog: 7 circuits, main circuit main
module main (
  input  [3:0] A,
  input  [3:0] B,
  output [3:0] Sum,
  output carry,
  output [3:0] subtract,
  output carry_2
);

  _4_bit_adder _4_bit_adder (.B(B), .A(A), .Carry(carry), .Sum(Sum));
  _4_bit_subtractor _4_bit_subtractor (.B(B), .A(A), .Carry(carry_2), .sub(subtract));
endmodule

module half_adder (
  input  A,
  input  B,
  output Sum,
  output Carry
);

  and and_1 (Carry, A, B);
  xor xor_1 (Sum, A, B);

  // Notes on the sheet:
  //   Half Adder
endmodule

module full_adder (
  input  A,
  input  B,
  input  C,
  output Sum,
  output Carry
);

  wire HA_2_carry, HA_carry, HA_sum;

  half_adder HA (.A(A), .B(B), .Sum(HA_sum), .Carry(HA_carry));
  half_adder HA_2 (.A(HA_sum), .B(C), .Sum(Sum), .Carry(HA_2_carry));
  or or_1 (Carry, HA_carry, HA_2_carry);

  // Notes on the sheet:
  //   Full Adder
endmodule

module _4_bit_adder_and_subtractor (
  input  [3:0] B,
  input  [3:0] A,
  input  Selection_bit,
  output out_4,
  output S3,
  output S2,
  output S1,
  output S0
);

  wire FA_2_carry, FA_3_carry, FA_4_carry, xor_1_out, xor_2_out, xor_3_out, xor_4_out;

  xor xor_1 (xor_1_out, Selection_bit, B[3]);
  full_adder FA (.A(A[3]), .B(xor_1_out), .C(FA_2_carry), .Sum(S3), .Carry(out_4));
  xor xor_2 (xor_2_out, Selection_bit, B[2]);
  full_adder FA_2 (.A(A[2]), .B(xor_2_out), .C(FA_3_carry), .Sum(S2), .Carry(FA_2_carry));
  xor xor_3 (xor_3_out, Selection_bit, B[1]);
  full_adder FA_3 (.A(A[1]), .B(xor_3_out), .C(FA_4_carry), .Sum(S1), .Carry(FA_3_carry));
  xor xor_4 (xor_4_out, Selection_bit, B[0]);
  full_adder FA_4 (.A(A[0]), .B(xor_4_out), .C(Selection_bit), .Sum(S0), .Carry(FA_4_carry));
endmodule

module _4_bit_subtractor (
  input  [3:0] B,
  input  [3:0] A,
  output Carry,
  output [3:0] sub
);

  _4_bit_adder_and_subtractor u_4_bit_adder_and_subtractor_1 (
    .out_4(Carry), .B(B), .A(A), .S3(sub[3]), .S2(sub[2]), .S1(sub[1]), .S0(sub[0]), .Selection_bit(1'b1));
endmodule

module _4_bit_adder (
  input  [3:0] B,
  input  [3:0] A,
  output Carry,
  output [3:0] Sum
);

  _4_bit_adder_and_subtractor u_4_bit_adder_and_subtractor_1 (
    .out_4(Carry), .B(B), .A(A), .S3(Sum[3]), .S2(Sum[2]), .S1(Sum[1]), .S0(Sum[0]), .Selection_bit(1'b0));
endmodule

module ALU (
  input  [3:0] A,
  input  [2:0] in_2,
  input  [3:0] B,
  input  in_4,
  input  in_5,
  output [7:0] out_6,
  output [3:0] out_7
);

  wire Adder_carry, Subtractor_carry;
  wire [2:0] comparator_out_3;
  wire [3:0] _2_s_complement_out_2, Adder_sum, bit_extender_1_out, bit_extender_2_out, divisor_quotient,
       divisor_reminder, multiplexer_1_out, shift_left_out_3, Subtractor_sub;
  wire [7:0] bit_extender_3_out, multiplier_out_3;

  Multiplexer #(.width(4), .enable("false")) multiplexer_1 (.in0(A), .in1(B), .out(multiplexer_1_out), .sel(in_4));
  _4_bit_adder Adder (.B(B), .A(A), .Carry(Adder_carry), .Sum(Adder_sum));
  _4_bit_subtractor Subtractor (.B(B), .A(A), .Carry(Subtractor_carry), .sub(Subtractor_sub));
  multiplier_main multiplier (.x(A), .y(B), .out_3(multiplier_out_3));
  division_main divisor (.divedend(A), .divisor(B), .Quotient(divisor_quotient), .REMINDER(divisor_reminder));
  Block comparator (
    .A(A), .B(B), .out_3(comparator_out_3[0]), .out_4(comparator_out_3[1]), .out_5(comparator_out_3[2]));
  _2S_Complement_main _2_s_complement (.in_1(multiplexer_1_out), .out_2(_2_s_complement_out_2));
  shifting_left_main shift_left (.in_2(1'b1), .out_3(shift_left_out_3), .in_1(multiplexer_1_out));
  assign bit_extender_1_out = {{3{1'b0}}, Adder_carry};  // Bit_Extender bit_extender_1
  assign bit_extender_2_out = {{3{1'b0}}, Subtractor_carry};  // Bit_Extender bit_extender_2
  Multiplexer #(.width(4), .enable("false")) multiplexer_2 (
    .in0(_2_s_complement_out_2), .in1(shift_left_out_3), .out(out_7), .sel(in_5));
  assign bit_extender_3_out = {{5{1'b0}}, comparator_out_3};  // Bit_Extender bit_extender_3
  Multiplexer #(.select(3), .width(8)) multiplexer_3 (
    .in0({bit_extender_1_out, Adder_sum}), .in1({bit_extender_2_out, Subtractor_sub}),
    .in2(multiplier_out_3), .in3({divisor_reminder, divisor_quotient}), .in4(bit_extender_3_out),
    .out(out_6), .sel(in_2));  // open: in5, in6, in7, en

  // Notes on the sheet:
  //   a<b
  //   a>b
  //   a=b
endmodule
