// Logisim project division.circ as structural Verilog: 2 circuits, main circuit main
module main (
  input  [3:0] divisor,
  input  [3:0] divedend,
  output [3:0] Quotient,
  output [3:0] REMINDER
);

  wire comparator_1_eq, comparator_1_lt, comparator_2_eq, comparator_2_lt, comparator_3_eq, comparator_3_lt,
       comparator_4_eq, comparator_4_lt;
  wire [3:0] bit_extender_1_out, bit_extender_2_out, bit_extender_3_out, bit_extender_4_out,
       bit_extender_5_out, bit_extender_6_out, bit_extender_7_out, multiplexer_1_out, multiplexer_2_out,
       multiplexer_3_out, multiplier_1_out, multiplier_2_out, multiplier_3_out, multiplier_4_out,
       shifter_1_out, shifter_2_out, shifter_3_out, subtractor_1_out, subtractor_2_out, subtractor_3_out;

  assign bit_extender_1_out = {{3{1'b0}}, divedend[3]};  // Bit_Extender bit_extender_1
  Multiplier #(.width(4)) multiplier_1 (
    .a(divisor), .b(bit_extender_2_out), .out(multiplier_1_out));  // open: cin, cout
  Comparator #(.width(4), .mode("unsigned")) comparator_1 (
    .a(divisor), .b(bit_extender_1_out), .eq(comparator_1_eq), .lt(comparator_1_lt));  // open: gt
  or or_1 (Quotient[3], comparator_1_eq, comparator_1_lt);
  Subtractor #(.width(4)) subtractor_1 (
    .a(bit_extender_1_out), .b(multiplier_1_out), .out(subtractor_1_out));  // open: bin, bout
  assign bit_extender_2_out = {{3{1'b0}}, Quotient[3]};  // Bit_Extender bit_extender_2
  Shifter #(.width(4)) shifter_1 (.in(subtractor_1_out), .\dist (2'b01), .out(shifter_1_out));
  assign bit_extender_3_out = {{2{1'b0}}, {subtractor_1_out[0], divedend[2]}};  // Bit_Extender bit_extender_3
  Multiplexer #(.width(4)) multiplexer_1 (
    .in0(shifter_1_out), .in1(bit_extender_3_out), .out(multiplexer_1_out), .sel(divedend[2]));  // open: en
  Comparator #(.width(4), .mode("unsigned")) comparator_2 (
    .a(divisor), .b(multiplexer_1_out), .eq(comparator_2_eq), .lt(comparator_2_lt));  // open: gt
  or or_2 (Quotient[2], comparator_2_eq, comparator_2_lt);
  assign bit_extender_4_out = {{3{1'b0}}, Quotient[2]};  // Bit_Extender bit_extender_4
  Subtractor #(.width(4)) subtractor_2 (
    .a(multiplexer_1_out), .b(multiplier_2_out), .out(subtractor_2_out));  // open: bin, bout
  Multiplier #(.width(4)) multiplier_2 (
    .a(bit_extender_4_out), .b(divisor), .out(multiplier_2_out));  // open: cin, cout
  Shifter #(.width(4)) shifter_2 (.in(subtractor_2_out), .\dist (2'b01), .out(shifter_2_out));
  assign bit_extender_5_out = {{1{1'b0}}, {subtractor_2_out[1:0], divedend[1]}};  // Bit_Extender bit_extender_5
  Multiplexer #(.width(4)) multiplexer_2 (
    .in0(shifter_2_out), .in1(bit_extender_5_out), .out(multiplexer_2_out), .sel(divedend[1]));  // open: en
  Comparator #(.width(4), .mode("unsigned")) comparator_3 (
    .a(divisor), .b(multiplexer_2_out), .eq(comparator_3_eq), .lt(comparator_3_lt));  // open: gt
  or or_3 (Quotient[1], comparator_3_eq, comparator_3_lt);
  assign bit_extender_6_out = {{3{1'b0}}, Quotient[1]};  // Bit_Extender bit_extender_6
  Subtractor #(.width(4)) subtractor_3 (
    .a(multiplexer_2_out), .b(multiplier_3_out), .out(subtractor_3_out));  // open: bin, bout
  Multiplier #(.width(4)) multiplier_3 (
    .a(bit_extender_6_out), .b(divisor), .out(multiplier_3_out));  // open: cin, cout
  Shifter #(.width(4)) shifter_3 (.in(subtractor_3_out), .\dist (2'b01), .out(shifter_3_out));
  Multiplexer #(.width(4)) multiplexer_3 (
    .in0(shifter_3_out), .in1({subtractor_3_out[2:0], divedend[0]}), .out(multiplexer_3_out),
    .sel(divedend[0]));  // open: en
  Comparator #(.width(4), .mode("unsigned")) comparator_4 (
    .a(divisor), .b(multiplexer_3_out), .eq(comparator_4_eq), .lt(comparator_4_lt));  // open: gt
  or or_4 (Quotient[0], comparator_4_eq, comparator_4_lt);
  assign bit_extender_7_out = {{3{1'b0}}, Quotient[0]};  // Bit_Extender bit_extender_7
  Subtractor #(.width(4)) subtractor_4 (
    .a(multiplexer_3_out), .b(multiplier_4_out), .out(REMINDER));  // open: bin, bout
  Multiplier #(.width(4)) multiplier_4 (
    .a(bit_extender_7_out), .b(divisor), .out(multiplier_4_out));  // open: cin, cout
endmodule

module div (
  input  [3:0] in_1,
  input  [3:0] in_2,
  output [3:0] out_3,
  output [3:0] out_4
);

  main main_1 (.divedend(in_1), .divisor(in_2), .Quotient(out_3), .REMINDER(out_4));
endmodule
