// Logisim project shifting_left.circ as structural Verilog: 2 circuits, main circuit main
module main (
  input  [3:0] in_1,
  input  in_2,
  output [3:0] out_3
);

  wire and_1_out, and_2_out, and_3_out, and_4_out, and_5_out, and_6_out, and_7_out, and_8_out, not_1_out,
       not_2_out, not_3_out, not_4_out;

  not not_1 (not_1_out, in_2);
  and and_1 (and_1_out, not_1_out, in_1[3]);
  or or_1 (out_3[3], and_1_out, and_2_out);
  and and_2 (and_2_out, in_2, in_1[2]);
  not not_2 (not_2_out, in_2);
  and and_3 (and_3_out, not_2_out, in_1[2]);
  or or_2 (out_3[2], and_3_out, and_4_out);
  and and_4 (and_4_out, in_2, in_1[1]);
  not not_3 (not_3_out, in_2);
  and and_5 (and_5_out, not_3_out, in_1[1]);
  or or_3 (out_3[1], and_5_out, and_6_out);
  and and_6 (and_6_out, in_2, in_1[0]);
  not not_4 (not_4_out, in_2);
  and and_7 (and_7_out, not_4_out, in_1[0]);
  and and_8 (and_8_out, in_2, 1'b0);
  or or_4 (out_3[0], and_7_out, and_8_out);

  // Notes on the sheet:
  //   bit 3
  //   bit 2
  //   bit 1
  //   bit 0
endmodule

module shifting (
);

  main main_1 ();  // open: in_2, out_3, in_1
endmodule
